# Fritzing sketch Garden-Snow-Blaster_Schaltplan (saved by Fritzing 0.9.9b)
breadboards: 1

parts:
  LCD1 = LCD screen
  Bauteil1 = Arduino Nano (Rev3.0)
  J1 = Basic Servo
  J2 = Basic Servo
  J3 = Basic Servo
  S1 = Pushbutton [package="[THT]"]
  S2 = Pushbutton [package="[THT]"]
  S3 = Pushbutton [package="[THT]"]
  S4 = Pushbutton [package="[THT]"]
  YF-S201_Flow_Meter1 = YF-S201 Water Flow Meter
  R1 = Resistor [tolerance=±5% power=0.25 resistance=220 package=THT]
  R2 = Resistor [tolerance=±5% power=0.25 resistance=220 package=THT]
  R3 = Resistor [tolerance=±5% power=0.25 resistance=220 package=THT]
  R4 = Resistor [tolerance=±5% power=0.25 resistance=10k package=THT]
  Bauteil2 = Barometric Pressure Sensor - BMP180 Breakout (GY-68)
  Bauteil3 = Bluetooth HC-05 Macho
  N2 = Netzteil [package="TO92 [THT]"]
  N1 = Netzteil [package="TO92 [THT]"]
  V1 = 230V Spannungsquelle [package="TO92 [THT]"]
  F3 = Leitungsschutzschalter [part_number=1 package="300 mil [THT]"]
  F1 = Leitungsschutzschalter [part_number=1 package="300 mil [THT]"]
  LED1 = LEDs [package=led10mm]
  M1 = DC Motor
  KY-1 = Keyes Relay [package=THT]
  KY-2 = Keyes Relay [package=THT]
  R5 = Rotary Potentiometer (Small) [maximum_resistance=100kΩ package=THT]
  LCM1602_IIC1 = LCM1602 IIC [part_number="LCM1602 IIC" chip_label="LCM1602 IIC" package="DIP (Dual Inline) [THT]"]

nets:
  VSS: LCD1.VSS, LCM1602_IIC1.VSS
  VDD: LCD1.VDD, LCM1602_IIC1.VDD
  N1: LCD1.V0, LCM1602_IIC1.V0
  N2: LCD1.RS, LCM1602_IIC1.RS
  N3: LCD1.R/W, LCM1602_IIC1.RW
  N4: LCD1.E, LCM1602_IIC1.E
  N5: LCD1.DB0, LCM1602_IIC1.D0
  N6: LCD1.DB1, LCM1602_IIC1.D1
  N7: LCD1.DB2, LCM1602_IIC1.D2
  N8: LCD1.DB3, LCM1602_IIC1.D3
  N9: LCD1.DB4, LCM1602_IIC1.D4
  N10: LCD1.DB5, LCM1602_IIC1.D5
  N11: LCD1.DB6, LCM1602_IIC1.D6
  N12: LCD1.DB7, LCM1602_IIC1.D7
  N13: LCD1.LED+, LCM1602_IIC1.A
  N14: LCD1.LED-, LCM1602_IIC1.K
  N15: Bauteil1.D2, S1.Pin_1, S1.Pin_2, R1.Pin_1
  N16: Bauteil1.D3, S2.Pin_1, S2.Pin_2, R2.Pin_1
  N17: Bauteil1.D4, Bauteil3.TXD
  N18: Bauteil1.D5, Bauteil3.RXD
  N19: Bauteil1.D6, J1.pulse
  N20: Bauteil1.D7, J2.pulse
  N21: Bauteil1.D8, KY-1.signal
  N22: Bauteil1.D9, S3.Pin_1, S3.Pin_2, R3.Pin_1
  N23: Bauteil1.D10, J3.pulse
  N24: Bauteil1.D11/MOSI, KY-2.signal
  N25: Bauteil1.D12/MISO, S4.Pin_1, S4.Pin_2, R4.Pin_1
  N26: Bauteil1.A5, Bauteil2.SCL, LCM1602_IIC1.SCL
  N27: Bauteil1.A4, Bauteil2.SDA, LCM1602_IIC1.SDA
  N28: Bauteil1.D13/SCK, YF-S201_Flow_Meter1.SIG
  GND: J1.gnd, J2.gnd, J3.gnd, YF-S201_Flow_Meter1.GND, R1.Pin_0, R2.Pin_0, R3.Pin_0, R4.Pin_0, Bauteil2.GND, Bauteil3.GND, N1.-, KY-1.ground, KY-2.ground, LCM1602_IIC1.GND
  VCC: J1.vcc, J2.vcc, J3.vcc, S1.Pin_3, S1.Pin_4, S2.Pin_3, S2.Pin_4, S3.Pin_3, S3.Pin_4, S4.Pin_3, S4.Pin_4, YF-S201_Flow_Meter1.VCC, Bauteil2.VCC, Bauteil3.VCC, N1.+, KY-1.power, KY-2.power, LCM1602_IIC1.VCC
  N29: N2.+, KY-2.C
  N30: N2.-, M1.pin_2, R5.leg2
  N31: N2.L, N1.L, F1.pin_2, KY-1.C
  N32: N2.G, N1.G, V1.G
  N33: N1.N, F3.pin_2, LED1.C
  N34: V1.L, F1.pin_1
  N35: V1.N, F3.pin_1
  N36: LED1.A, KY-1.NC, KY-1.NO
  N37: M1.pin_1, R5.wiper
  N38: KY-2.NC, R5.leg1

notes:
  Netzteil 24V
  Netzteil 5V
  Spannungsversorgung 230V

custom parts:
  YF-S201 Water Flow Meter: The YF-S201 Flow Meter. The input voltage is 5V to 24V (DC).
  230V Spannungsquelle: Spannungsquelle
  Leitungsschutzschalter: Sicherung/Leitungsschutzschalter
  Keyes Relay: The Keyes 5V relay module is suitable for SCM development, home appliance control. It uses a 5V~12V TIL control signal which can control DC / AC signal.
  LCM1602 IIC: I2C-Module to use a 1602 or 2004 LCD on with the wire.h libory Serial LCD Modul
